# Fritzing sketch RGB5050 (saved by Fritzing 0.9.3b)
circuit board: 8.46667cm x 5.64444cm
breadboards: 1

parts:
  Q1 = Basic FET N-Channel [package="TO220 [THT]"]
  WeMos_D1_Mini1 = WeMos D1 Mini
  IC1 = Voltage Regulator [package=to220-igo]
  Q2 = Basic FET N-Channel [package="TO220 [THT]"]
  Q3 = Basic FET N-Channel [package="TO220 [THT]"]
  J2 = Power Jack [package=power_jack_pth]
  JP1 = Header 6 [package=1x06-smd]
  R1 = Resistor [tolerance=±5% resistance=220 package="1206 [SMD]"]
  R2 = Resistor [tolerance=±5% resistance=220 package="1206 [SMD]"]
  R3 = Resistor [tolerance=±5% resistance=220 package="1206 [SMD]"]

nets:
  N1: Q1.gate, R1.Pin_1
  N2: Q1.drain, JP1.6
  GND: Q1.source, WeMos_D1_Mini1.G, IC1.GND, Q2.source, Q3.source, J2.GND
  N3: WeMos_D1_Mini1.5V, IC1.OUT
  N4: WeMos_D1_Mini1.D1, R1.Pin_0
  N5: WeMos_D1_Mini1.D2, R2.Pin_1
  N6: WeMos_D1_Mini1.D3, R3.Pin_1
  N7: IC1.IN, J2.PWR, JP1.3
  N8: Q2.gate, R2.Pin_0
  N9: Q2.drain, JP1.5
  N10: Q3.gate, R3.Pin_0
  N11: Q3.drain, JP1.4
